# Fritzing sketch mqtt-multinode (saved by Fritzing 0.9.2b)
breadboards: 1

parts:
  U1 = NodeMCU V1.0
  DHT1 = DHT22 Humidity and Temperature Sensor
  R1 = Resistor [tolerance=±5% resistance=220 package=THT]
  PIR1 = PIR sensor
  KY-1 = Keyes Relay [package=THT]

nets:
  3V3: U1.3V3, DHT1.VDD, R1.Pin_1, KY-1.power
  GND: U1.GND, DHT1.GND, PIR1.GND, KY-1.ground
  N1: U1.D5, DHT1.DATA, R1.Pin_0
  N2: U1.D6, KY-1.signal
  N3: U1.D7, PIR1.SIG
  VIN: U1.Vin, PIR1.VDD

notes:
  Not the actual relay module I'm using, but looks close. Mine works at 3.3V, signal is active-low.
  FLASH button connected to GPIO 0
  Make sure PIR motion sensor output is 3.3V

custom parts:
  NodeMCU V1.0: ESP9266 based NodeMCU
  Keyes Relay: The Keyes 5V relay module is suitable for SCM development, home appliance control. It uses a 5V~12V TIL control signal which can control DC / AC signal.
